// Logisim project Votingmachine.circ as structural Verilog: 1 circuit, main circuit main
module main (
  input  in_1,
  input  in_2,
  input  in_3,
  input  in_4,
  output out_5
);

  wire and_1_out, and_2_out, and_3_out, or_1_out, or_2_out, xor_1_out, xor_2_out, xor_3_out;

  xor xor_1 (xor_1_out, in_1, in_2);
  and and_1 (and_1_out, in_1, in_2);
  xor xor_2 (xor_2_out, xor_1_out, in_3);
  buf and_2 (and_2_out, in_3);  // AND_Gate
  or or_1 (or_1_out, and_1_out, and_2_out);
  xor xor_3 (xor_3_out, xor_2_out, in_4);
  buf and_3 (and_3_out, xor_2_out);  // AND_Gate
  or or_2 (or_2_out, xor_3_out, and_3_out);
  and and_4 (out_5, or_2_out, or_1_out);
endmodule
